# Fritzing sketch s4d (saved by Fritzing 0.9.3b)
breadboards: 2

parts:
  U1 = POT [package=pot_alpha_rv16af-20]
  U2 = POT [package=pot_alpha_rv16af-20]
  LED1 = RGB LED (com. anode, rbg) [package="5 mm [THT]"]
  S2 = Pushbutton [package="[THT]"]
  S3 = Pushbutton [package="[THT]"]
  S4 = Pushbutton [package="[THT]"]
  LED2 = RGB LED (com. anode, rbg) [package="5 mm [THT]"]
  J1 = Piezo Speaker
  R7 = Resistor [tolerance=±20% resistance=100 package=THT]
  R8 = Resistor [tolerance=±20% resistance=100 package=THT]
  R9 = Resistor [tolerance=±20% resistance=100 package=THT]
  S5 = Pushbutton [package="[THT]"]
  S6 = Pushbutton [package="[THT]"]
  S7 = Pushbutton [package="[THT]"]
  U3 = POT [package=pot_alpha_rv16af-20]  # not connected
  U4 = POT [package=pot_alpha_rv16af-20]  # not connected
  LED3 = RGB LED (com. anode, rbg) [package="5 mm [THT]"]  # not connected
  LED4 = RGB LED (com. anode, rbg) [package="5 mm [THT]"]  # not connected
  Onderdeel1 = Arduino Uno (Rev3)
  Onderdeel2 = Arduino Uno (Rev3)
  R2 = Resistor [tolerance=±5% resistance=220 package="2512 [SMD]"]
  R1 = Resistor [tolerance=±5% resistance=220 package="2512 [SMD]"]
  R5 = Resistor [tolerance=±5% resistance=220 package="2512 [SMD]"]
  R6 = Resistor [tolerance=±5% resistance=220 package="2512 [SMD]"]
  R4 = Resistor [tolerance=±5% resistance=220 package="2512 [SMD]"]
  R3 = Resistor [tolerance=±5% resistance=220 package="2512 [SMD]"]

nets:
  N1: U1.A, U2.A, LED1.blue_cathode, S2.Pin_1, S2.Pin_2, S3.Pin_1, S3.Pin_2, S4.Pin_1, S4.Pin_2, LED2.blue_cathode, Onderdeel1.5V
  N2: U1.S, Onderdeel1.A1
  N3: U1.E, U2.E, R8.Pin_1, R9.Pin_1, Onderdeel1.GND
  N4: U2.S, Onderdeel1.A0
  N5: LED1.red_cathode, R1.Pin_1
  N6: LED1.common_anode, R3.Pin_1
  N7: LED1.green_cathode, R2.Pin_1
  N8: S2.Pin_3, S2.Pin_4, R7.Pin_0, Onderdeel1.D2
  N9: S3.Pin_3, S3.Pin_4, R8.Pin_0, Onderdeel1.D7
  N10: S4.Pin_3, S4.Pin_4, R9.Pin_0, Onderdeel1.D8
  N11: LED2.red_cathode, R4.Pin_1
  N12: LED2.common_anode, R5.Pin_1
  N13: LED2.green_cathode, R6.Pin_1
  N14: J1.pin2, Onderdeel2.D4
  N15: S5.Pin_1, S5.Pin_2
  N16: S5.Pin_3, S5.Pin_4
  N17: S6.Pin_1, S6.Pin_2
  N18: S6.Pin_3, S6.Pin_4
  N19: S7.Pin_1, S7.Pin_2
  N20: S7.Pin_3, S7.Pin_4
  N21: Onderdeel1.D9_PWM, R6.Pin_0
  N22: Onderdeel1.D10_PWM/SS, R5.Pin_0
  N23: Onderdeel1.D11_PWM/MOSI, R4.Pin_0
  N24: Onderdeel1.D3_PWM, R2.Pin_0
  N25: Onderdeel1.D5_PWM, R3.Pin_0
  N26: Onderdeel1.D6_PWM, R1.Pin_0

notes:
  Vooraanzicht
  Let op.
  De buzzer kon er niet in één keer bij. Deze is apart getekend.
  Alles moet op één bord.
  Het lange pootje bij de led is de tweede van links (in deze view).
  De led is hieronder getekend zoals de pootjes in het bord zitten.
  O
  | | | |
  | | |
  | |
  |
